# Fritzing sketch grow_box (saved by Fritzing 0.9.0b)
circuit board: 16.3216cm x 8.54504cm
perfboards: 1
breadboards: 1

parts:
  Part1 = Arduino Uno (Rev3)
  U1 = mystery part, 3 pins [chip_label="power supply"]
  R1 = Resistor [tolerance=±5% resistance=6.8k package=THT]
  Q2 = NPN-Transistor [package="TO92 [THT]"]
  Q1 = Basic FET P-Channel [package="TO220 [THT]"]
  R3 = Resistor [tolerance=±5% resistance=10k package=THT]
  U2 = Luxeon LED [package=luxeon]
  U3 = Luxeon LED [package=luxeon]
  U4 = Luxeon LED [package=luxeon]
  R4 = Resistor [tolerance=±5% resistance=6.8 package=THT]
  U5 = Luxeon LED [package=luxeon]
  U6 = Luxeon LED [package=luxeon]
  U7 = Luxeon LED [package=luxeon]
  R5 = Resistor [tolerance=±5% resistance=6.8 package=THT]
  R6 = Resistor [tolerance=±5% resistance=10k package=THT]
  DHT1 = DHT22 Humidity and Temperature Sensor

nets:
  N1: Part1.D3_PWM, R6.Pin_1
  N2: Part1.D6_PWM, R1.Pin_0, DHT1.DATA
  GND: Part1.GND, U1.pin3, Q2.E, R4.Pin_0, R5.Pin_0, DHT1.GND
  12V: Part1.VIN, U1.pin1, Q1.drain, R3.Pin_1
  5V: U1.pin2, R1.Pin_1, DHT1.VDD
  N3: Q2.B, R6.Pin_0
  N4: Q2.C, Q1.gate, R3.Pin_0
  N5: Q1.source, U4.A, U7.A
  N6: U2.A, U4.C
  N7: U2.C, U3.A
  N8: U3.C, R4.Pin_1
  N9: U5.A, U7.C
  N10: U5.C, U6.A
  N11: U6.C, R5.Pin_1
